# Fritzing sketch ESP32_DHT11_GPIO19 (saved by Fritzing 0.9.3b)

parts:
  MH-ET_LIVE_ESP32_DEVKIT1 = MH-ET LIVE ESP32 DEVKIT 38 pins
  DHT1 = DHT11 Humitidy and Temperature Sensor
  R1 = Resistor [tolerance=±5% resistance=220 package=THT]

nets:
  N1: MH-ET_LIVE_ESP32_DEVKIT1.3V3, R1.Pin_1
  GND: MH-ET_LIVE_ESP32_DEVKIT1.GND, DHT1.GND
  N2: MH-ET_LIVE_ESP32_DEVKIT1.IO19, DHT1.DATA, R1.Pin_0

custom parts:
  MH-ET LIVE ESP32 DEVKIT 38 pins: http://mh.nodebb.com/topic/2/mh-et-live-esp32-devkit
  DHT11 Humitidy and Temperature Sensor: DHT11 Humidity and Temperature Sensor
