# Fritzing sketch ESP32_MPU6050 (saved by Fritzing 0.9.3b)

parts:
  MH-ET_LIVE_ESP32_DEVKIT1 = MH-ET LIVE ESP32 DEVKIT 38 pins
  Part1 = InvenSense MPU6050

nets:
  3V3: MH-ET_LIVE_ESP32_DEVKIT1.3V3, Part1.VCC
  GND: MH-ET_LIVE_ESP32_DEVKIT1.GND, Part1.GND
  N1: MH-ET_LIVE_ESP32_DEVKIT1.IO22, Part1.SCL
  N2: MH-ET_LIVE_ESP32_DEVKIT1.IO21, Part1.SDA

custom parts:
  MH-ET LIVE ESP32 DEVKIT 38 pins: http://mh.nodebb.com/topic/2/mh-et-live-esp32-devkit
