# Fritzing sketch DHT11_ILI9341_SPI_ESP32_Schematic (saved by Fritzing 0.9.3b)

parts:
  MH-ET_LIVE_ESP32_DEVKIT1 = MH-ET LIVE ESP32 DEVKIT 38 pins
  DHT1 = DHT11 Humitidy and Temperature Sensor
  LCD1 = 2.8" SPI TFT Module [part_number=MSP2807]

nets:
  N1: MH-ET_LIVE_ESP32_DEVKIT1.3V3, LCD1.pin1, LCD1.pin4, LCD1.pin8
  N2: MH-ET_LIVE_ESP32_DEVKIT1.IO12, DHT1.DATA
  5V: MH-ET_LIVE_ESP32_DEVKIT1.5V, DHT1.VDD
  GND: MH-ET_LIVE_ESP32_DEVKIT1.GND, DHT1.GND
  N3: MH-ET_LIVE_ESP32_DEVKIT1.IO23, LCD1.pin6
  N4: MH-ET_LIVE_ESP32_DEVKIT1.IO19, LCD1.pin9
  N5: MH-ET_LIVE_ESP32_DEVKIT1.IO18, LCD1.pin7
  N6: MH-ET_LIVE_ESP32_DEVKIT1.IO5, LCD1.pin3
  N7: MH-ET_LIVE_ESP32_DEVKIT1.IO0, LCD1.pin5
  N8: MH-ET_LIVE_ESP32_DEVKIT1.IO2, LCD1.pin11

custom parts:
  MH-ET LIVE ESP32 DEVKIT 38 pins: http://mh.nodebb.com/topic/2/mh-et-live-esp32-devkit
  DHT11 Humitidy and Temperature Sensor: DHT11 Humidity and Temperature Sensor
  2.8" SPI TFT Module: A generic 2.8 inch LCD TFT 320x240 display with touchscreen and SD card slot. Uses the ILI9341 controller, like the Adafruit displays of this size uses.
